# Fritzing sketch wiring finpro edspertid (saved by Fritzing 0.9.3b)

parts:
  U2 = ESP8266 NodeMCU LoLin base
  ZS-042_RTC1 = ZS-042 RTC Module
  U4 = 4-Channel 5v Relay Shield [package=relay-4ch5v10a]
  LED8 = LEDs [package=led10mm]
  LED9 = LEDs [package=led10mm]
  LED10 = LEDs [package=led10mm]
  LED11 = LEDs [package=led10mm]
  U5 = SWITCH-SPST-2 [package=switch-spst-vertical]
  U6 = SWITCH-SPST-2 [package=switch-spst-vertical]
  U7 = SWITCH-SPST-2 [package=switch-spst-vertical]
  U8 = SWITCH-SPST-2 [package=switch-spst-vertical]

nets:
  N1: U2.D0-0, U2.D0-3, U8.P
  N2: U2.D1-3, ZS-042_RTC1.SCL
  N3: U2.D2-3, ZS-042_RTC1.SDA
  N4: U2.D3-0, U2.D3-3, U5.P
  N5: U2.D4-0, U2.D4-3, U6.P
  N6: U2.D5-0, U2.D5-3, U7.P
  N7: U2.D6-0, U2.D6-2, U4.IN1
  N8: U2.D7-0, U2.D7-2, U4.IN2
  N9: U2.D8-0, U2.D8-2, U4.IN3
  N10: U2.RX-0, U2.RX-2, U4.IN4
  VCC: U2.VIN, U2.5V-0, U2.5V-1, U2.5V-3, ZS-042_RTC1.VCC, U4.VCC
  GND: U2.GND8-5, U2.GND8-7, U2.GND8-8, ZS-042_RTC1.GND, U4.GND, U5.O, U6.O, U7.O, U8.O
  N11: U4.K1-On, LED11.A
  N12: U4.K2-On, LED10.A
  N13: U4.K3-On, LED9.A
  N14: U4.K4-On, LED8.A

notes:
  240V

custom parts:
  ESP8266 NodeMCU LoLin base: ESP8266 based NodeMCU Base
  4-Channel 5v Relay Shield: 4 Channel 5v Relay Shield w. 2x SPD-06VDC-SD-C
  LEDs: LEDs Standard schematic elements and footprints for 5mm, 3mm, 1206, and 0603 sized LEDs. 5mm - Spark Fun Electronics SKU : COM-00529 (and others)
